# Fritzing sketch stopwatch (saved by Fritzing 0.9.6b)
breadboards: 2

parts:
  Part1 = Arduino Uno (Rev3)
  U1 = 7-SEGMENT-DISPLAY [package=7-segment-display]
  U2 = 7-SEGMENT-DISPLAY [package=7-segment-display]
  Q2 = NPN-Transistor [package="TO92 [THT]"]
  Q3 = NPN-Transistor [package="TO92 [THT]"]
  R1 = Resistor [tolerance=±5% resistance=220 package="1206 [SMD]"]
  R2 = Resistor [tolerance=±5% resistance=220 package="1206 [SMD]"]
  R3 = Resistor [tolerance=±5% resistance=220 package="1206 [SMD]"]
  R4 = Resistor [tolerance=±5% resistance=220 package="1206 [SMD]"]
  R5 = Resistor [tolerance=±5% resistance=220 package="1206 [SMD]"]
  R6 = Resistor [tolerance=±5% resistance=220 package="1206 [SMD]"]
  R7 = Resistor [tolerance=±5% resistance=220 package="1206 [SMD]"]
  R8 = Resistor [tolerance=±5% resistance=220 package="1206 [SMD]"]
  R9 = Resistor [tolerance=±5% resistance=220 package="1206 [SMD]"]
  R10 = Resistor [tolerance=±5% resistance=220 package="1206 [SMD]"]
  S1 = Pushbutton [package="[THT]"]
  S2 = Pushbutton [package="[THT]"]
  S3 = Pushbutton [package="[THT]"]
  S4 = Pushbutton [package="[THT]"]
  S5 = Pushbutton [package="[THT]"]

nets:
  N1: Part1.A0, S5.Pin_1, S5.Pin_2
  N2: Part1.A1, S4.Pin_1, S4.Pin_2
  N3: Part1.A3, S3.Pin_1, S3.Pin_2
  N4: Part1.A4/SDA, S2.Pin_1, S2.Pin_2
  N5: Part1.A5/SCL, S1.Pin_1, S1.Pin_2
  N6: Part1.D8, R4.Pin_0
  N7: Part1.D9_PWM, R3.Pin_0
  N8: Part1.D10_PWM/SS, R2.Pin_1
  N9: Part1.D11_PWM/MOSI, R1.Pin_1
  N10: Part1.GND, Q2.E, Q3.E, S1.Pin_3, S1.Pin_4, S2.Pin_3, S2.Pin_4, S3.Pin_3, S3.Pin_4, S4.Pin_3, S4.Pin_4, S5.Pin_3, S5.Pin_4
  N11: Part1.D2, Part1.D3_PWM, R10.Pin_0
  N12: Part1.D4, R9.Pin_0
  N13: Part1.D5_PWM, R7.Pin_0
  N14: Part1.D6_PWM, R6.Pin_0
  N15: Part1.D7, R5.Pin_0
  N16: U1.E, U2.E, R3.Pin_1
  N17: U1.D, U2.D, R7.Pin_1
  N18: U1.G1, U2.G1, R8.Pin_1
  N19: U1.C, U1.F, Q3.C
  N20: U1.DP, U2.DP, R9.Pin_1
  N21: U1.B, U2.B, R10.Pin_1
  N22: U1.A, U2.A, R6.Pin_1
  N23: U1.G2, U2.G2, R5.Pin_1
  N24: U1.G, U2.G, R4.Pin_1
  N25: U2.C, U2.F, Q2.C
  N26: Q2.B, R2.Pin_0
  N27: Q3.B, R1.Pin_0
